# Fritzing sketch circuit (saved by Fritzing 0.8.7b)
breadboards: 1

parts:
  M1 = Stepper Motor - Bipolar  # not connected
  Power_plug1 = Power plug
  DRV_1 = DRV 8825 Stepper Motor Carrier, High Current [part_number="DRV 8825"]  # not connected
  DC1 = DC_DC_XL4016 [chip_label=XL4016 package=board_screw]  # not connected
  DC2 = DC_DC_XL4016 [package=board_screw]
  Raspberry_Pi_1 = Raspberry Pi 3 [part_number=RPI-3-V1.2]
  3-pins_Hall_Effect_Sensor1 = mystery part, 3 pins [chip_label="Hall Effect Sensor"]
  Part1 = Adafruit ADS1115 16Bit I2C ADC [part_number="Adafruit #1085"]
  U7 = RF-LINK_RX [package=rf-link_rx]

nets:
  N1: Power_plug1.GND, DC2.IN-
  N2: Power_plug1.VCC, DC2.IN+
  N3: DC2.OUT+, Raspberry_Pi_1.5V
  GND: DC2.OUT-, Raspberry_Pi_1.GND, 3-pins_Hall_Effect_Sensor1.pin2, Part1.GND, U7.GND
  3V3: Raspberry_Pi_1.3v3, 3-pins_Hall_Effect_Sensor1.pin3, Part1.VDD, U7.VCC
  N4: Raspberry_Pi_1.GPIO2, Part1.SCL
  N5: Raspberry_Pi_1.GPIO3, Part1.SDA
  N6: Raspberry_Pi_1.GIPO22, U7.Data#2
  N7: 3-pins_Hall_Effect_Sensor1.pin1, Part1.AIN0

notes:
  12V
  5V
  3.3V

custom parts:
  DC_DC_XL4016: DC-DC Converter step down voltage regulator XL4016 custom sketch.
  Adafruit ADS1115 16Bit I2C ADC: For microcontrollers without an analog-to-digital converter or when you want a higher-precision ADC, the ADS1115 provides 16-bit precision at 860 samples/second over I2C. The chip can be configured as 4 single-ended input channels, or two differential channels. As a nice bonus, it even includes a programmable gain amplifier, up to x16, to help boost up smaller single/differential signals to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
  RF-LINK_RX: RF Link receivers- WRL-8947, 8948, 8949, 8950
